# Fritzing sketch Lesson 10 Controlling LED by Potentiometer (saved by Fritzing 0.9.3b)
breadboards: 1

parts:
  LED_RED = LED - 5mm [color="Red (633nm)" package="5 mm [THT]"]
  R1 = Resistor [tolerance=±5% resistance=220 package=THT]
  R4 = Potentiometer [package=THT]
  元件3 = Uno R4

nets:
  N1: LED_RED.cathode, R4.leg2, 元件3.GND
  N2: LED_RED.anode, R1.Pin_0
  N3: R1.Pin_1, 元件3.D9_PWM
  N4: R4.leg1, 元件3.5V
  N5: R4.wiper, 元件3.A0

notes:
  220Ω
  +
  -

custom parts:
  Potentiometer: A standard adjustable resistor (potentiometer).
  Uno R4: The Sunfounder Uno is a microcontroller board based on the ATmega328 (datasheet). It has 14 digital input/output pins (of which 6 can be used as PWM outputs), 6 analog inputs, a 16 MHz ceramic resonator, a USB connection, a power jack, an ICSP header, and a reset button. It contains everything needed to support the microcontroller; simply connect it to a computer with a USB cable or power it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
