# Fritzing sketch Lesson 14 Thermistor (saved by Fritzing 0.9.3b)
breadboards: 1

parts:
  Thermistor = Temperature Sensor (Thermistor) [thermistor_type=NTC package=THT]
  R6 = Resistor [tolerance=±5% resistance=10k package=THT]
  LCD1 = LCD screen
  R8 = Potentiometer [package=THT]
  元件2 = SunFounder Uno R3
  元件3 = Uno R4

nets:
  VDD: Thermistor.pin_0, LCD1.VDD, R8.leg1, 元件3.5V
  N1: Thermistor.pin_1, R6.Pin_0, 元件3.A0
  VSS: R6.Pin_1, LCD1.VSS, LCD1.R/W, LCD1.LED-, R8.leg2, 元件3.GND
  N2: LCD1.V0, R8.wiper
  N3: LCD1.E, 元件2.D6_PWM
  N4: LCD1.DB4, 元件3.D10_PWM/SS
  N5: LCD1.DB5, 元件3.D11_PWM/MOSI
  N6: LCD1.DB6, 元件3.D12/MISO
  N7: LCD1.DB7, 元件3.D13/SCK
  N8: LCD1.LED+, 元件3.3V3

notes:
  103
  10KΩ

custom parts:
  LCD screen: A standard character display, usually with 2x16 characters. Comes in many colors.
  Potentiometer: A standard adjustable resistor (potentiometer).
  SunFounder Uno R3: The Sunfounder Uno is a microcontroller board based on the ATmega328 (datasheet). It has 14 digital input/output pins (of which 6 can be used as PWM outputs), 6 analog inputs, a 16 MHz ceramic resonator, a USB connection, a power jack, an ICSP header, and a reset button. It contains everything needed to support the microcontroller; simply connect it to a computer with a USB cable or power it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
  Uno R4: The Sunfounder Uno is a microcontroller board based on the ATmega328 (datasheet). It has 14 digital input/output pins (of which 6 can be used as PWM outputs), 6 analog inputs, a 16 MHz ceramic resonator, a USB connection, a power jack, an ICSP header, and a reset button. It contains everything needed to support the microcontroller; simply connect it to a computer with a USB cable or power it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
