# Fritzing sketch Lesson 17 Humiture Sensor (saved by Fritzing 0.9.3b)
breadboards: 1

parts:
  S1 = Humiture Sensor v1.0 [package=THT]
  LCD1 = LCD screen
  R3 = Potentiometer [package=THT]
  元件3 = Uno R4

nets:
  VDD: S1.S, LCD1.VDD, R3.leg2, 元件3.5V
  N1: S1.+, 元件3.D3_PWM
  N2: S1.-, LCD1.R/W, LCD1.LED-, R3.leg1, 元件3.GND
  N3: LCD1.V0, R3.wiper
  N4: LCD1.RS, 元件3.D4
  N5: LCD1.E, 元件3.D6_PWM
  N6: LCD1.DB4, 元件3.D10_PWM/SS
  N7: LCD1.DB5, 元件3.D11_PWM/MOSI
  N8: LCD1.DB6, 元件3.D12/MISO
  N9: LCD1.DB7, 元件3.D13/SCK
  N10: LCD1.LED+, 元件3.3V3

custom parts:
  Humiture Sensor v1.0: Humiture Sensor www.sunfounder.com
  LCD screen: A standard character display, usually with 2x16 characters. Comes in many colors.
  Potentiometer: A standard adjustable resistor (potentiometer).
  Uno R4: The Sunfounder Uno is a microcontroller board based on the ATmega328 (datasheet). It has 14 digital input/output pins (of which 6 can be used as PWM outputs), 6 analog inputs, a 16 MHz ceramic resonator, a USB connection, a power jack, an ICSP header, and a reset button. It contains everything needed to support the microcontroller; simply connect it to a computer with a USB cable or power it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
