# Fritzing sketch Lesson 18 Joystick PS2 (saved by Fritzing 0.9.3b)

parts:
  S1 = Joystick PS2 v1.0 [package=THT]
  元件3 = Uno R4

nets:
  GND: S1.GND, 元件3.GND
  VCC: S1.VCC, 元件3.5V
  N1: S1.VRX, 元件3.A0
  N2: S1.VRY, 元件3.A1
  N3: S1.SW, 元件3.D8

custom parts:
  Joystick PS2 v1.0: A joystick is an input device consisting of a stick that pivots on a base and reports its angle or direction to the device it is controlling. Joysticks are often used to control video games and robots. A Joystick PS2 is used here.
  Uno R4: The Sunfounder Uno is a microcontroller board based on the ATmega328 (datasheet). It has 14 digital input/output pins (of which 6 can be used as PWM outputs), 6 analog inputs, a 16 MHz ceramic resonator, a USB connection, a power jack, an ICSP header, and a reset button. It contains everything needed to support the microcontroller; simply connect it to a computer with a USB cable or power it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
