# Fritzing sketch Lesson 22 Simple Creation-Stopwatch (saved by Fritzing 0.9.3b)
breadboards: 1

parts:
  LED2 = 7-SEGMENT-4DIGIT-YOUNGSUN [package=7-segment-4digit-youngsun-longpads]
  R1 = Resistor [tolerance=±5% resistance=220 package=THT]
  R7 = Resistor [tolerance=±5% resistance=220 package=THT]
  R6 = Resistor [tolerance=±5% resistance=220 package=THT]
  R8 = Resistor [tolerance=±5% resistance=220 package=THT]
  R5 = Resistor [tolerance=±5% resistance=220 package=THT]
  R4 = Resistor [tolerance=±5% resistance=220 package=THT]
  R3 = Resistor [tolerance=±5% resistance=220 package=THT]
  R2 = Resistor [tolerance=±5% resistance=220 package=THT]
  元件3 = Uno R4

nets:
  N1: LED2.DIG2, R4.Pin_1
  N2: LED2.D, R5.Pin_1
  N3: LED2.COL-A, R7.Pin_0
  N4: LED2.E, R6.Pin_0
  N5: LED2.DIG3, R8.Pin_0
  N6: LED2.DP, 元件3.D10_PWM/SS
  N7: LED2.APOS-A, R1.Pin_0
  N8: LED2.F, 元件3.D11_PWM/MOSI
  N9: LED2.COL-C, 元件3.ICSP_MISO, 元件3.D12/MISO
  N10: LED2.C, R2.Pin_1
  N11: LED2.A, R3.Pin_1
  N12: LED2.G, 元件3.D13/SCK
  N13: R1.Pin_1, 元件3.D3_PWM
  N14: R7.Pin_1, 元件3.D9_PWM
  N15: R6.Pin_1, 元件3.D4
  N16: R8.Pin_1, 元件3.D8
  N17: R5.Pin_0, 元件3.D5_PWM
  N18: R4.Pin_0, 元件3.D6_PWM
  N19: R3.Pin_0, 元件3.D2
  N20: R2.Pin_0, 元件3.D7

notes:
  220Ω

custom parts:
  7-SEGMENT-4DIGIT-YOUNGSUN: This is a part for the 4-Digit 7-segment LEDs from Young Sun. Different from the Digikey LEDs, all 16 pins are used. The LONGPADS Variant is used for a test jig, but you may like it because there is more pad to solder to. If you are concerned about routing space, the standard works just fine though.
  Uno R4: The Sunfounder Uno is a microcontroller board based on the ATmega328 (datasheet). It has 14 digital input/output pins (of which 6 can be used as PWM outputs), 6 analog inputs, a 16 MHz ceramic resonator, a USB connection, a power jack, an ICSP header, and a reset button. It contains everything needed to support the microcontroller; simply connect it to a computer with a USB cable or power it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
