# Fritzing sketch Lesson 24 Simple Creation-Small Fan (saved by Fritzing 0.9.3b)
circuit board: 8.46667cm x 5.64444cm
breadboards: 1

parts:
  IC1 = L293D [package=THT]
  M1 = DC Motor
  R6 = Resistor [tolerance=±5% resistance=10k package=THT]
  S3 = Pushbutton [package="[THT]"]
  C1 = Capacitor [package=cap-pth-small2]
  元件3 = Uno R4

nets:
  N1: IC1.Enable_1, IC1.+Vmotor, IC1.+V, S3.Pin_1, S3.Pin_2, 元件3.5V
  N2: IC1.In_1, 元件3.D10_PWM/SS
  N3: IC1.Out_1_(_Controlled_by_Enable_1_), M1.pin_2
  N4: IC1.0V, R6.Pin_0, C1.1, 元件3.GND
  N5: IC1.Out_2_(_Controlled_by_Enable_1_), M1.pin_1
  N6: IC1.In_2, 元件3.D9_PWM
  N7: R6.Pin_1, S3.Pin_3, S3.Pin_4, C1.2, 元件3.D2

notes:
  10KΩ
  104

custom parts:
  Pushbutton: A generic pushbutton.
  Capacitor: Capacitor Standard 0603 ceramic capacitor, and 0.1 leaded capacitor.
  Uno R4: The Sunfounder Uno is a microcontroller board based on the ATmega328 (datasheet). It has 14 digital input/output pins (of which 6 can be used as PWM outputs), 6 analog inputs, a 16 MHz ceramic resonator, a USB connection, a power jack, an ICSP header, and a reset button. It contains everything needed to support the microcontroller; simply connect it to a computer with a USB cable or power it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
