# Fritzing sketch Lesson 3 Blinking LED (saved by Fritzing 0.9.3b)
breadboards: 1

parts:
  LED1 = LED - 5mm [color="Red (633nm)" package="5 mm [THT]"]
  R1 = Resistor [tolerance=±5% resistance=220 package=THT]
  元件2 = Uno R4

nets:
  N1: LED1.cathode, 元件2.GND
  N2: LED1.anode, R1.Pin_1
  N3: R1.Pin_0, 元件2.D9_PWM

notes:
  220Ω
  +
  -

custom parts:
  Uno R4: The Sunfounder Uno is a microcontroller board based on the ATmega328 (datasheet). It has 14 digital input/output pins (of which 6 can be used as PWM outputs), 6 analog inputs, a 16 MHz ceramic resonator, a USB connection, a power jack, an ICSP header, and a reset button. It contains everything needed to support the microcontroller; simply connect it to a computer with a USB cable or power it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
