# Fritzing sketch Lesson 4 Flowing LED Lights (saved by Fritzing 0.9.3b)
breadboards: 1

parts:
  LED1 = LED - 5mm [color="Green (570nm)" package="5 mm [THT]"]
  LED3 = LED - 5mm [color="Yellow (595nm)" package="5 mm [THT]"]
  LED4 = LED - 5mm [color="Red (633nm)" package="5 mm [THT]"]
  LED7 = LED - 5mm [color="Red (633nm)" package="5 mm [THT]"]
  R2 = Resistor [tolerance=±5% resistance=220 package=THT]
  R3 = Resistor [tolerance=±5% resistance=220 package=THT]
  R4 = Resistor [tolerance=±5% resistance=220 package=THT]
  R6 = Resistor [tolerance=±5% resistance=220 package=THT]
  R5 = Resistor [tolerance=±5% resistance=220 package=THT]
  R7 = Resistor [tolerance=±5% resistance=220 package=THT]
  R8 = Resistor [tolerance=±5% resistance=220 package=THT]
  元件2 = SunFounder Uno R3  # not connected
  R9 = Resistor [tolerance=±5% resistance=220 package=THT]
  LED9 = LED - 5mm [color="Green (570nm)" package="5 mm [THT]"]
  LED10 = LED - 5mm [color="Yellow (595nm)" package="5 mm [THT]"]
  LED11 = LED - 5mm [color="Green (570nm)" package="5 mm [THT]"]
  LED12 = LED - 5mm [color="Red (633nm)" package="5 mm [THT]"]
  元件3 = Uno R4

nets:
  N1: LED1.cathode, LED3.cathode, LED4.cathode, LED7.cathode, LED9.cathode, LED10.cathode, LED11.cathode, LED12.cathode, 元件3.GND
  N2: LED1.anode, R3.Pin_0
  N3: LED3.anode, R2.Pin_0
  N4: LED4.anode, R6.Pin_0
  N5: LED7.anode, R9.Pin_0
  N6: R2.Pin_1, 元件3.D7
  N7: R3.Pin_1, 元件3.D8
  N8: R4.Pin_0, LED9.anode
  N9: R4.Pin_1, 元件3.D6_PWM
  N10: R6.Pin_1, 元件3.D5_PWM
  N11: R5.Pin_0, LED10.anode
  N12: R5.Pin_1, 元件3.D4
  N13: R7.Pin_0, LED11.anode
  N14: R7.Pin_1, 元件3.D3_PWM
  N15: R8.Pin_0, LED12.anode
  N16: R8.Pin_1, 元件3.D2
  N17: R9.Pin_1, 元件3.D9_PWM

notes:
  220Ω
  +
  -

custom parts:
  SunFounder Uno R3: The Sunfounder Uno is a microcontroller board based on the ATmega328 (datasheet). It has 14 digital input/output pins (of which 6 can be used as PWM outputs), 6 analog inputs, a 16 MHz ceramic resonator, a USB connection, a power jack, an ICSP header, and a reset button. It contains everything needed to support the microcontroller; simply connect it to a computer with a USB cable or power it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
  Uno R4: The Sunfounder Uno is a microcontroller board based on the ATmega328 (datasheet). It has 14 digital input/output pins (of which 6 can be used as PWM outputs), 6 analog inputs, a 16 MHz ceramic resonator, a USB connection, a power jack, an ICSP header, and a reset button. It contains everything needed to support the microcontroller; simply connect it to a computer with a USB cable or power it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
