# Fritzing sketch Lesson 8 Relay (saved by Fritzing 0.9.3b)
breadboards: 1

parts:
  Q1 = NPN-Transistor [package="TO92 [THT]"]
  D1 = Rectifier Diode [part_number=1N4001 package="300 mil [THT]"]
  LED1 = LED - 5mm [color="Red (633nm)" package="5 mm [THT]"]
  R3 = Resistor [tolerance=±5% resistance=1k package=THT]
  R2 = Resistor [tolerance=±5% resistance=220 package=THT]
  K1 = Relay [part_number=FRS1B-S package=THT]
  元件3 = Uno R4

nets:
  N1: Q1.E, LED1.cathode, 元件3.GND
  N2: Q1.B, R3.Pin_0
  N3: Q1.C, D1.anode, K1.COIL1
  N4: D1.cathode, K1.C1, K1.C2, K1.COIL2, 元件3.5V
  N5: LED1.anode, R2.Pin_1
  N6: R3.Pin_1, 元件3.D8
  N7: R2.Pin_0, K1.B

notes:
  220Ω
  +
  -
  1KΩ

custom parts:
  Relay: An SPDT relay.
  Uno R4: The Sunfounder Uno is a microcontroller board based on the ATmega328 (datasheet). It has 14 digital input/output pins (of which 6 can be used as PWM outputs), 6 analog inputs, a 16 MHz ceramic resonator, a USB connection, a power jack, an ICSP header, and a reset button. It contains everything needed to support the microcontroller; simply connect it to a computer with a USB cable or power it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
