# Fritzing sketch Lesson 9 RGB LED (saved by Fritzing 0.9.3b)
breadboards: 1

parts:
  LED1 = RGB LED (com. anode, rbg) [package="5 mm [THT]"]
  R2 = Resistor [tolerance=±5% resistance=220 package=THT]
  R3 = Resistor [tolerance=±5% resistance=220 package=THT]
  R1 = Resistor [tolerance=±5% resistance=220 package=THT]
  元件3 = Uno R4

nets:
  N1: LED1.red_cathode, R1.Pin_1
  N2: LED1.common_anode, 元件3.GND
  N3: LED1.blue_cathode, R3.Pin_1
  N4: LED1.green_cathode, R2.Pin_1
  N5: R2.Pin_0, 元件3.D9_PWM
  N6: R3.Pin_0, 元件3.D10_PWM/SS
  N7: R1.Pin_0, 元件3.D11_PWM/MOSI

notes:
  220Ω
  R
  G
  B

custom parts:
  Uno R4: The Sunfounder Uno is a microcontroller board based on the ATmega328 (datasheet). It has 14 digital input/output pins (of which 6 can be used as PWM outputs), 6 analog inputs, a 16 MHz ceramic resonator, a USB connection, a power jack, an ICSP header, and a reset button. It contains everything needed to support the microcontroller; simply connect it to a computer with a USB cable or power it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
